# Fritzing sketch obstacleavoiding (saved by Fritzing 1.0.6)

parts:
  L298N1 = L298N DC motor driver
  M1 = DC Motor [voltage_(max)=6V voltage_(min)=3V]
  M2 = DC Motor [voltage_(max)=6V voltage_(min)=3V]
  Part1 = Arduino Uno (Rev3)
  U1 = LIPO-2000mAh [package=lipo-2000]
  U2 = LIPO-2000mAh [package=lipo-2000]
  M3 = DC Motor [voltage_(max)=6V voltage_(min)=3V]  # not connected
  M4 = DC Motor [voltage_(max)=6V voltage_(min)=3V]  # not connected
  HC-SR04_Sensor_1 = HC-SR04 Ultrasonic Distance Sensor
  M5 = Dagu DGServo 9g (Top view) [part_number=RS001B]
  M6 = RioRand LM2596

nets:
  N1: L298N1.OUT1, M2.pin_2
  N2: L298N1.OUT2, M2.pin_1
  N3: L298N1.OUT3, M1.pin_2
  N4: L298N1.OUT4, M1.pin_1
  N5: L298N1.12V, U1.+, M6.Pin_1
  GND: L298N1.GND, Part1.GND, HC-SR04_Sensor_1.GND, M6.Pin_2
  N6: L298N1.ENA, Part1.D11_PWM/MOSI
  N7: L298N1.ENB, Part1.D3_PWM
  N8: L298N1.IN1, Part1.D12/MISO
  N9: L298N1.IN2, Part1.D13/SCK
  N10: L298N1.IN3, Part1.D7
  N11: L298N1.IN4, Part1.D6_PWM
  N12: Part1.D8, M5.pulse
  N13: Part1.D4, HC-SR04_Sensor_1.ECHO
  N14: Part1.D5_PWM, HC-SR04_Sensor_1.TRIG
  5V: Part1.5V, HC-SR04_Sensor_1.VCC
  N15: U1.-, U2.+
  N16: M5.gnd, M6.Pin_4
  N17: M5.vcc, M6.Pin_3

notes:
  Left Motor
  Right Motor
  L298N Motor Driver Board

custom parts:
  L298N DC motor driver: 2x DC motor driver with 78M05 positive voltage regulator (7..35 V) L298N: max 46 V, 2 A Set 5 V Enable jumper to enable 5 V regultor (needed for the L298N) and +5 V output at screw terminal or supply external +5 V at screw terminal Set ENA and/or ENB to +5 V to enable motor permanently or supply ENA and/or ENB with PWM signal IN1 and IN2 set rotation directory for motor A (OUT1/OUT2) IN2 and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
